# Fritzing sketch finlays_load_sensor_modules_board (saved by Fritzing 0.9.3b)
circuit board: 2.28cm x 3.04cm
circuit board: 3.04cm x 2.28cm
circuit board: 2.28cm x 3.04cm
circuit board: 2.28cm x 3.04cm
circuit board: 3.04cm x 2.28cm
circuit board: 3.04cm x 2.28cm
circuit board: 3.04cm x 2.28cm
circuit board: 2.28cm x 3.04cm
circuit board: 9.82362cm x 6.4325cm
circuit board: 9.62058cm x 4.88338cm
circuit board: 3.04cm x 2.28cm
circuit board: 3.04cm x 2.28cm
circuit board: 2.28cm x 3.04cm
circuit board: 2.28cm x 3.04cm
breadboards: 1

parts:
  J2 = female pin header, 5 pins [form="♀ (female)"]  # not connected
  J1 = female pin header, 5 pins [form="♀ (female)"]  # not connected
  J3 = female pin header, 5 pins [form="♀ (female)"]  # not connected
  J4 = female pin header, 5 pins [form="♀ (female)"]  # not connected
  J5 = female pin header, 5 pins [form="♀ (female)"]  # not connected
  J6 = female pin header, 5 pins [form="♀ (female)"]  # not connected
  J7 = female pin header, 5 pins [form="♀ (female)"]  # not connected
  J8 = female pin header, 5 pins [form="♀ (female)"]  # not connected
  J9 = female pin header, 5 pins [form="♀ (female)"]  # not connected
  J10 = female pin header, 5 pins [form="♀ (female)"]  # not connected
  J11 = female pin header, 5 pins [form="♀ (female)"]  # not connected
  J12 = female pin header, 5 pins [form="♀ (female)"]  # not connected
  J13 = female pin header, 5 pins [form="♀ (female)"]
  J14 = female pin header, 5 pins [form="♀ (female)"]
  J15 = female pin header, 5 pins [form="♀ (female)"]
  J16 = female pin header, 5 pins [form="♀ (female)"]
  J17 = female pin header, 5 pins [form="♀ (female)"]
  J18 = female pin header, 5 pins [form="♀ (female)"]
  J30 = female pin header, 5 pins [form="♀ (female)"]
  J32 = female pin header, 5 pins [form="♀ (female)"]
  J33 = female pin header, 5 pins [form="♀ (female)"]
  J31 = female pin header, 4 pins [form="♀ (female)"]
  J34 = female pin header, 4 pins [form="♀ (female)"]
  J35 = female pin header, 4 pins [form="♀ (female)"]
  J36 = female pin header, 5 pins [form="♀ (female)"]
  J37 = female pin header, 5 pins [form="♀ (female)"]
  J38 = female pin header, 5 pins [form="♀ (female)"]
  J39 = female pin header, 5 pins [form="♀ (female)"]
  J40 = female pin header, 5 pins [form="♀ (female)"]
  J41 = female pin header, 5 pins [form="♀ (female)"]
  J42 = female pin header, 4 pins [form="♀ (female)"]
  J43 = female pin header, 4 pins [form="♀ (female)"]
  J44 = female pin header, 4 pins [form="♀ (female)"]
  J45 = female pin header, 5 pins [form="♀ (female)"]
  J46 = female pin header, 5 pins [form="♀ (female)"]
  J47 = female pin header, 5 pins [form="♀ (female)"]

nets:
  N1: J13.pin2, J15.pin2, J17.pin2, J31.pin1, J34.pin1, J35.pin1
  N2: J13.pin3, J31.pin2
  N3: J13.pin4, J31.pin3
  N4: J13.pin5, J15.pin5, J17.pin5, J31.pin4, J34.pin4, J35.pin4
  N5: J14.pin1, J30.pin1
  N6: J14.pin2, J30.pin2
  N7: J14.pin3, J30.pin3
  N8: J14.pin4, J30.pin4
  N9: J14.pin5, J30.pin5
  N10: J15.pin3, J34.pin2
  N11: J15.pin4, J34.pin3
  N12: J16.pin1, J32.pin1
  N13: J16.pin2, J32.pin2
  N14: J16.pin3, J32.pin3
  N15: J16.pin4, J32.pin4
  N16: J16.pin5, J32.pin5
  N17: J17.pin3, J35.pin2
  N18: J17.pin4, J35.pin3
  N19: J18.pin1, J33.pin1
  N20: J18.pin2, J33.pin2
  N21: J18.pin3, J33.pin3
  N22: J18.pin4, J33.pin4
  N23: J18.pin5, J33.pin5
  N24: J36.pin2, J37.pin2, J38.pin2, J42.pin1, J43.pin1, J44.pin1
  N25: J36.pin3, J43.pin2
  N26: J36.pin4, J43.pin3
  N27: J36.pin5, J37.pin5, J38.pin5, J42.pin4, J43.pin4, J44.pin4
  N28: J37.pin3, J44.pin2
  N29: J37.pin4, J44.pin3
  N30: J38.pin3, J42.pin2
  N31: J38.pin4, J42.pin3
  N32: J39.pin1, J45.pin1
  N33: J39.pin2, J45.pin2
  N34: J39.pin3, J45.pin3
  N35: J39.pin4, J45.pin4
  N36: J39.pin5, J45.pin5
  N37: J40.pin1, J46.pin1
  N38: J40.pin2, J46.pin2
  N39: J40.pin3, J46.pin3
  N40: J40.pin4, J46.pin4
  N41: J40.pin5, J46.pin5
  N42: J41.pin1, J47.pin1
  N43: J41.pin2, J47.pin2
  N44: J41.pin3, J47.pin3
  N45: J41.pin4, J47.pin4
  N46: J41.pin5, J47.pin5

notes:
  VCC
  GND
  DAT
  CLK
  RED
  BLK
  WHT
  GRN
  YLW
